# Fritzing sketch simon-says-edison (saved by Fritzing 0.9.3b)
breadboards: 1

parts:
  S1 = Pushbutton [package="[THT]"]
  R1 = Resistor [tolerance=±5% resistance=220 package=THT]
  R2 = Resistor [tolerance=±5% resistance=10k package=THT]
  LED1 = LED - 5mm [color="Blue (470nm)" package="5 mm [THT]"]
  S2 = Pushbutton [package="[THT]"]
  S3 = Pushbutton [package="[THT]"]
  S4 = Pushbutton [package="[THT]"]
  LED2 = LED - 5mm [color="Red (635nm)" package="5 mm [THT]"]
  LED3 = LED - 5mm [color="Yellow (585nm)" package="5 mm [THT]"]
  LED4 = LED - 5mm [color="Green (555nm)" package="5 mm [THT]"]
  R3 = Resistor [tolerance=±5% resistance=10k package=THT]
  R4 = Resistor [tolerance=±5% resistance=10k package=THT]
  R5 = Resistor [tolerance=±5% resistance=10k package=THT]
  R6 = Resistor [tolerance=±5% resistance=220 package=THT]
  R7 = Resistor [tolerance=±5% resistance=220 package=THT]
  R8 = Resistor [tolerance=±5% resistance=220 package=THT]
  Part2 = Intel Edison Arduinobreakout

nets:
  N1: S1.Pin_1, S1.Pin_2, LED1.anode, Part2.D3_PWM
  N2: S1.Pin_3, S1.Pin_4, S2.Pin_3, S2.Pin_4, S3.Pin_3, S3.Pin_4, S4.Pin_3, S4.Pin_4, Part2.5V
  N3: R1.Pin_0, R2.Pin_0, R3.Pin_0, R4.Pin_0, R5.Pin_0, R6.Pin_0, R8.Pin_0, Part2.GND
  N4: R1.Pin_1, LED1.cathode
  N5: R2.Pin_1, Part2.D2
  N6: S2.Pin_1, S2.Pin_2, R3.Pin_1, Part2.D4
  N7: S3.Pin_1, S3.Pin_2, R4.Pin_1, Part2.D6_PWM
  N8: S4.Pin_1, S4.Pin_2, R5.Pin_1, Part2.D8
  N9: LED2.cathode, R6.Pin_1
  N10: LED2.anode, Part2.D5_PWM
  N11: LED3.cathode, R7.Pin_1
  N12: LED3.anode, Part2.D7
  N13: LED4.cathode, R8.Pin_1
  N14: LED4.anode, Part2.D9_PWM
